// Digital circuit cpu.dig as structural Verilog
module cpu (
  input  clk,
  input  HLT,
  output [31:0] OUT1,
  output [31:0] OUT2,
  output [31:0] RegINBus,
  output [1:0] out_5,
  output [31:0] RegOUTBus,
  output [31:0] MemoryAddressBus,
  output [11:0] out_9,
  output [31:0] MemoryOUTBus,
  output out_11
);

  wire add_1_c_o, and_1_out, and_3_out, comparator_1_eq, comparator_2_eq, comparator_3_eq, comparator_5_eq,
       d_ff_3_q, decoder_1_out_1, decoder_1_out_2, decoder_1_out_3, decoder_1_out_4, decoder_1_out_5,
       decoder_1_out_6, decoder_1_out_7, decoder_1_out_8, decoder_1_out_9, decoder_1_out_10,
       decoder_1_out_11, decoder_1_out_12, decoder_1_out_13, decoder_1_out_14, decoder_1_out_15,
       decoder_2_out_0, decoder_2_out_1, decoder_2_out_2, decoder_2_out_3, decoder_2_out_4, decoder_2_out_5,
       decoder_2_out_6, decoder_2_out_7, decoder_2_out_8, decoder_2_out_9, decoder_2_out_10,
       decoder_2_out_11, decoder_2_out_12, decoder_2_out_13, decoder_2_out_14, decoder_2_out_15,
       decoder_3_out_0, decoder_3_out_1, decoder_3_out_2, decoder_3_out_3, decoder_3_out_4, decoder_3_out_5,
       decoder_3_out_6, decoder_3_out_7, decoder_3_out_8, decoder_3_out_9, decoder_3_out_10,
       decoder_3_out_11, decoder_3_out_12, decoder_3_out_13, decoder_3_out_14, decoder_3_out_15,
       decoder_4_out_1, decoder_4_out_2, decoder_4_out_3, demultiplexer_7_out_0, demultiplexer_7_out_1,
       demultiplexer_11_out_0, demultiplexer_11_out_1, IRSwitcher_out, not_1_out, not_2_out, not_3_out,
       not_4_out, or_1_out, or_2_out, or_3_out, or_6_out, pulldown_1_out, pulldown_23_out, pulldown_24_out,
       pulldown_33_out, pulldown_34_out, pulldown_37_out, pullup_1_out, pullup_2_out, pullup_3_out;
  wire [0:0] not_5_out, not_6_out, not_7_out, or_9_out, pulldown_5_out, sub_2_c_o;
  wire [1:0] or_8_out, or_8_out_2, or_8_out_3, or_8_out_4, or_10_out, pulldown_27_out, pulldown_39_out,
       pulldown_45_out;
  wire [1:1] and_2_out, comparator_4_eq;
  wire [2:0] demultiplexer_8_out_0, multiplexer_6_out_4;
  wire [3:0] demultiplexer_9_out_0, multiplexer_6_out;
  wire [4:0] demultiplexer_4_out_0, demultiplexer_5_out_1, demultiplexer_6_out_0, demultiplexer_9_out_1,
       multiplexer_6_out_3, multiplexer_6_out_5, multiplexer_6_out_6;
  wire [5:5] comparator_6_eq;
  wire [6:0] demultiplexer_1_out_0, demultiplexer_2_out_1, demultiplexer_3_out_0, multiplexer_8_out,
       or_5_out, pulldown_10_out;
  wire [7:0] demultiplexer_8_out_1;
  wire [9:0] demultiplexer_4_out_1;
  wire [11:0] demultiplexer_5_out_0;
  wire [12:0] multiplexer_7_out, pulldown_4_out;
  wire [30:0] pulldown_41_out, pulldown_42_out, pulldown_43_out, pulldown_44_out, pulldown_46_out,
       pulldown_47_out;
  wire [31:0] add_2_s, add_3_s, and_4_out, barrelshifter_1_out, barrelshifter_2_out, barrelshifter_3_out,
       bitextender_1_out, bitextender_2_out, bitextender_3_out, bitextender_4_out, counterpreset_1_out,
       d_ff_1_q, d_ff_2_q, d_ff_4_q, d_ff_5_q, d_ff_6_q, d_ff_7_q, d_ff_8_q, d_ff_9_q, d_ff_10_q, d_ff_11_q,
       d_ff_12_q, d_ff_13_q, d_ff_14_q, d_ff_15_q, d_ff_16_q, d_ff_17_q, d_ff_18_q, demultiplexer_10_out_0,
       demultiplexer_10_out_1, multiplexer_1_out, multiplexer_2_out, multiplexer_3_out, multiplexer_4_out,
       multiplexer_5_out, multiplexer_9_out, multiplexer_10_out, multiplexer_11_out, multiplexer_12_out,
       multiplexer_13_out, multiplexer_14_out, multiplexer_15_out, multiplexer_16_out, multiplexer_17_out,
       multiplexer_18_out, multiplexer_19_out, multiplexer_20_out, multiplexer_21_out, multiplexer_22_out,
       multiplexer_23_out, multiplexer_24_out, multiplexer_25_out, multiplexer_26_out, multiplexer_27_out,
       multiplexer_28_out, multiplexer_29_out, multiplexer_30_out, or_4_out, or_7_out, pulldown_2_out,
       pulldown_3_out, pulldown_30_out, pulldown_40_out, rom_1_d, sub_1_s, sub_2_s, xor_1_out;
  wire [31:6] multiplexer_6_out_2;

  or or_1 (or_1_out, comparator_5_eq, comparator_1_eq);
  PullUp pullup_1 (.out(pullup_1_out));
  PullDown pulldown_1 (.out(pulldown_1_out));
  Comparator #(.Bits(4)) comparator_1 (.a(multiplexer_6_out), .b(4'b1100), .eq(comparator_1_eq));  // open: gt, lt
  Demultiplexer #(.Bits(7)) demultiplexer_1 (
    .sel(or_2_out), .in(multiplexer_6_out_2[31:25]), .out_0(demultiplexer_1_out_0),
    .out_1({pulldown_2_out[31], demultiplexer_4_out_1[9:4]}));
  Demultiplexer #(.Bits(7)) demultiplexer_2 (
    .sel(or_1_out), .in(demultiplexer_1_out_0), .out_0(demultiplexer_5_out_0[11:5]),
    .out_1(demultiplexer_2_out_1));
  Demultiplexer #(.Bits(7)) demultiplexer_3 (
    .sel(comparator_5_eq), .in(demultiplexer_2_out_1), .out_0(demultiplexer_3_out_0),
    .out_1({pulldown_4_out[12], pulldown_4_out[10:5]}));
  Counter IRSwitcher (.en(pullup_1_out), .C(not_1_out), .clr(pulldown_1_out), .out(IRSwitcher_out));  // open: ovf
  Demultiplexer #(.Bits(5)) demultiplexer_4 (
    .sel(or_2_out), .in(multiplexer_6_out_6), .out_0(demultiplexer_4_out_0),
    .out_1({demultiplexer_4_out_1[3:0], pulldown_2_out[20]}));
  Demultiplexer #(.Bits(5)) demultiplexer_5 (
    .sel(or_1_out), .in(demultiplexer_4_out_0), .out_0(demultiplexer_5_out_0[4:0]),
    .out_1(demultiplexer_5_out_1));
  PullUp pullup_2 (.out(pullup_2_out));
  Demultiplexer #(.Bits(5)) demultiplexer_6 (
    .sel(or_2_out), .in(multiplexer_6_out_5), .out_0(demultiplexer_6_out_0),
    .out_1(demultiplexer_8_out_1[7:3]));
  Multiplexer #(.Bits(32)) multiplexer_1 (
    .sel(demultiplexer_7_out_0), .in_0(d_ff_1_q), .in_1(multiplexer_5_out), .out(multiplexer_1_out));
  Demultiplexer demultiplexer_7 (
    .sel(IRSwitcher_out), .in(pullup_2_out), .out_0(demultiplexer_7_out_0), .out_1(demultiplexer_7_out_1));
  Demultiplexer #(.Bits(3)) demultiplexer_8 (
    .sel(or_2_out), .in(multiplexer_6_out_4), .out_0(demultiplexer_8_out_0),
    .out_1(demultiplexer_8_out_1[2:0]));
  D_FF #(.Bits(32)) d_ff_1 (.D(multiplexer_1_out), .C(not_1_out), .Q(d_ff_1_q));  // open: nQ
  or or_2 (or_2_out, comparator_4_eq[1], or_3_out);
  or or_3 (or_3_out, comparator_3_eq, comparator_2_eq);
  BitExtender #(.inputBits(20), .outputBits(32)) bitextender_1 (
    .in({pulldown_2_out[31], demultiplexer_4_out_1, pulldown_2_out[20], demultiplexer_8_out_1}),
    .out(bitextender_1_out));
  PullDown #(.Bits(12)) pulldown_2 (.out(pulldown_2_out[11:0]));
  BitExtender #(.inputBits(21), .outputBits(32)) bitextender_2 (
    .in({pulldown_2_out[31], demultiplexer_8_out_1, pulldown_2_out[20], demultiplexer_4_out_1, pulldown_5_out[0]}),
    .out(bitextender_2_out));
  BitExtender #(.inputBits(12), .outputBits(32)) bitextender_3 (.in(demultiplexer_5_out_0), .out(bitextender_3_out));
  Comparator #(.Bits(4)) comparator_2 (.a(multiplexer_6_out), .b(4'b1101), .eq(comparator_2_eq));  // open: gt, lt
  Comparator #(.Bits(4)) comparator_3 (.a(multiplexer_6_out), .b(4'b0101), .eq(comparator_3_eq));  // open: gt, lt
  Comparator #(.Bits(4)) comparator_4 (.a(multiplexer_6_out), .b(4'b1011), .eq(comparator_4_eq[1]));  // open: gt, lt
  Multiplexer #(.Selector_Bits(2), .Bits(32)) multiplexer_2 (
    .sel({comparator_4_eq[1], rom_1_d[21]}), .in_0(bitextender_1_out),
    .in_1({pulldown_2_out[31], demultiplexer_4_out_1, pulldown_2_out[20], demultiplexer_8_out_1, pulldown_2_out[11:0]}),
    .in_2(bitextender_2_out), .in_3(pulldown_3_out), .out(multiplexer_2_out));
  PullDown #(.Bits(32)) pulldown_3 (.out(pulldown_3_out));
  Multiplexer #(.Bits(32)) multiplexer_3 (
    .sel(demultiplexer_7_out_1), .in_0(d_ff_2_q), .in_1(multiplexer_5_out), .out(multiplexer_3_out));
  assign RegOUTBus = rom_1_d[17] ? or_4_out : 32'bz;  // Driver driver_1
  D_FF #(.Bits(32)) d_ff_2 (.D(multiplexer_3_out), .C(not_1_out), .Q(d_ff_2_q));  // open: nQ
  Multiplexer #(.Bits(32)) multiplexer_4 (
    .sel(IRSwitcher_out), .in_0(d_ff_2_q), .in_1(d_ff_1_q), .out(multiplexer_4_out));
  PullDown pulldown_4 (.out(pulldown_4_out[0]));
  PullDown pulldown_5 (.out(pulldown_5_out[0]));
  BitExtender #(.inputBits(13), .outputBits(32)) bitextender_4 (.in(multiplexer_7_out), .out(bitextender_4_out));
  assign or_4_out = bitextender_4_out | multiplexer_2_out | bitextender_3_out;  // Or or_4, 32 bits wide
  RAMDualPort #(.AddrBits(20), .isProgramMemory("true"), .Bits(32)) ramdualport_1 (
    .A(MemoryAddressBus[19:0]), .Din(RegINBus), .str(rom_1_d[20]), .C(clk), .ld(rom_1_d[19]), .D(MemoryOUTBus));
  Multiplexer #(.Bits(32)) multiplexer_5 (
    .sel(rom_1_d[18]), .in_0(MemoryOUTBus), .in_1(32'h13), .out(multiplexer_5_out));
  Multiplexer #(.Bits(32)) multiplexer_6 (
    .sel(d_ff_3_q), .in_0(multiplexer_4_out), .in_1(32'h13),
    .out({multiplexer_6_out_2[31:25], multiplexer_6_out_6, multiplexer_6_out_5, multiplexer_6_out_4, multiplexer_6_out_3, multiplexer_6_out_2[6], multiplexer_6_out, out_5}));
  Demultiplexer #(.Bits(5)) demultiplexer_9 (
    .sel(comparator_5_eq), .in(multiplexer_6_out_3), .out_0({out_11, demultiplexer_9_out_0}),
    .out_1(demultiplexer_9_out_1));
  Multiplexer #(.Bits(13)) multiplexer_7 (
    .sel(and_1_out), .in_0({{2{pulldown_4_out[12]}}, pulldown_4_out[10:5], demultiplexer_9_out_1}),
    .in_1({pulldown_4_out[12], demultiplexer_9_out_1[0], pulldown_4_out[10:5], demultiplexer_9_out_1[4:1], pulldown_4_out[0]}),
    .out(multiplexer_7_out));
  ROM #(.AddrBits(9), .Bits(32)) rom_1 (
    .A({demultiplexer_8_out_0, comparator_6_eq[5], multiplexer_6_out_2[6], multiplexer_6_out}), .sel(1'b1),
    .D(rom_1_d));
  PullDown pulldown_6 (.out(rom_1_d[23]));
  PullDown pulldown_7 (.out(rom_1_d[24]));
  Comparator #(.Bits(4)) comparator_5 (.a(multiplexer_6_out), .b(4'b1000), .eq(comparator_5_eq));  // open: gt, lt
  PullDown pulldown_8 (.out(rom_1_d[21]));
  PullDown pulldown_9 (.out(rom_1_d[22]));
  not not_1 (not_1_out, clk);
  and and_1 (and_1_out, comparator_5_eq, multiplexer_6_out_2[6]);
  Multiplexer #(.Bits(7)) multiplexer_8 (
    .sel(or_1_out), .in_0(RegOUTBus[11:5]), .in_1(pulldown_10_out), .out(multiplexer_8_out));
  PullDown #(.Bits(7)) pulldown_10 (.out(pulldown_10_out));
  assign or_5_out = multiplexer_8_out | demultiplexer_3_out_0;  // Or or_5, 7 bits wide
  Comparator #(.Bits(7)) comparator_6 (.a(or_5_out), .b(7'b0100000), .eq(comparator_6_eq[5]));  // open: gt, lt
  assign RegINBus = rom_1_d[23] ? MemoryOUTBus : 32'bz;  // Driver driver_2
  assign RegINBus = rom_1_d[22] ? RegOUTBus : 32'bz;  // Driver driver_3
  PullDown pulldown_11 (.out(rom_1_d[19]));
  PullDown pulldown_12 (.out(rom_1_d[20]));
  PullDown pulldown_13 (.out(rom_1_d[17]));
  PullDown pulldown_14 (.out(rom_1_d[18]));
  PullDown pulldown_15 (.out(rom_1_d[15]));
  PullDown pulldown_16 (.out(rom_1_d[16]));
  PullDown pulldown_17 (.out(rom_1_d[13]));
  PullDown pulldown_18 (.out(rom_1_d[14]));
  PullDown pulldown_19 (.out(rom_1_d[11]));
  PullDown pulldown_20 (.out(rom_1_d[12]));
  Multiplexer #(.Bits(32)) multiplexer_9 (.sel(rom_1_d[14]), .in_0(RegOUTBus), .in_1(OUT2), .out(multiplexer_9_out));
  assign RegINBus = rom_1_d[24] ? OUT2 : 32'bz;  // Driver driver_4
  PullDown pulldown_21 (.out(rom_1_d[10]));
  PullDown pulldown_22 (.out(rom_1_d[9]));
  D_FF d_ff_3 (.D(HLT), .C(not_2_out), .Q(d_ff_3_q));  // open: nQ
  not not_2 (not_2_out, clk);
  Sub #(.Bits(32)) sub_1 (.a(MemoryOUTBus), .b(32'h1), .c_i(pulldown_23_out), .s(sub_1_s));  // open: c_o
  PullDown pulldown_23 (.out(pulldown_23_out));
  Decoder #(.Selector_Bits(4)) decoder_1 (
    .sel(demultiplexer_9_out_0), .out_1(decoder_1_out_1), .out_2(decoder_1_out_2), .out_3(decoder_1_out_3),
    .out_4(decoder_1_out_4), .out_5(decoder_1_out_5), .out_6(decoder_1_out_6), .out_7(decoder_1_out_7),
    .out_8(decoder_1_out_8), .out_9(decoder_1_out_9), .out_10(decoder_1_out_10), .out_11(decoder_1_out_11),
    .out_12(decoder_1_out_12), .out_13(decoder_1_out_13), .out_14(decoder_1_out_14), .out_15(decoder_1_out_15));  // open: out_0
  Add #(.Bits(2)) add_1 (.a(OUT1[1:0]), .b(multiplexer_9_out[1:0]), .c_i(pulldown_24_out), .c_o(add_1_c_o));  // open: s
  PullDown pulldown_24 (.out(pulldown_24_out));
  PullDown pulldown_25 (.out(rom_1_d[8]));
  PullDown pulldown_26 (.out(rom_1_d[7]));
  not not_3 (not_3_out, RegINBus[0]);
  PullDown #(.Bits(2)) pulldown_27 (.out(pulldown_27_out));
  PullDown pulldown_28 (.out(rom_1_d[5]));
  PullDown pulldown_29 (.out(rom_1_d[6]));
  Multiplexer #(.Selector_Bits(2), .Bits(32)) multiplexer_10 (
    .sel({and_2_out[1], rom_1_d[16]}), .in_0(32'h1), .in_1({{3{RegOUTBus[31]}}, RegOUTBus[30:2]}),
    .in_2(32'h1), .in_3(32'h1), .out(multiplexer_10_out));
  and and_2 (and_2_out[1], not_3_out, rom_1_d[16]);
  Multiplexer #(.Bits(32)) multiplexer_11 (
    .sel(not_4_out), .in_0(sub_1_s), .in_1(counterpreset_1_out), .out(multiplexer_11_out));
  or or_6 (or_6_out, not_4_out, rom_1_d[1]);
  not not_4 (not_4_out, rom_1_d[0]);
  Multiplexer #(.Selector_Bits(2), .Bits(32)) multiplexer_12 (
    .sel({rom_1_d[3], rom_1_d[4]}), .in_0(OUT1), .in_1(MemoryAddressBus),
    .in_2({pulldown_27_out, OUT1[31:2]}), .in_3(pulldown_30_out), .out(multiplexer_12_out));
  PullDown #(.Bits(32)) pulldown_30 (.out(pulldown_30_out));
  Multiplexer #(.Bits(32)) multiplexer_13 (
    .sel(rom_1_d[5]), .in_0(multiplexer_9_out), .in_1({{3{multiplexer_9_out[31]}}, multiplexer_9_out[30:2]}),
    .out(multiplexer_13_out));
  and and_3 (and_3_out, rom_1_d[3], rom_1_d[5], add_1_c_o);
  PullDown pulldown_31 (.out(rom_1_d[4]));
  PullDown pulldown_32 (.out(rom_1_d[3]));
  CounterPreset #(.Bits(32), .isProgramCounter("true")) counterpreset_1 (
    .en(pullup_3_out), .C(clk), .dir(pulldown_33_out), .in(multiplexer_11_out), .ld(or_6_out),
    .clr(d_ff_3_q), .out(counterpreset_1_out));  // open: ovf
  PullUp pullup_3 (.out(pullup_3_out));
  PullDown pulldown_33 (.out(pulldown_33_out));
  PullDown pulldown_34 (.out(pulldown_34_out));
  PullDown pulldown_35 (.out(rom_1_d[2]));
  PullDown pulldown_36 (.out(rom_1_d[1]));
  Add #(.Bits(32)) add_2 (
    .a(MemoryAddressBus), .b(multiplexer_10_out), .c_i(pulldown_37_out), .s(add_2_s));  // open: c_o
  PullDown pulldown_37 (.out(pulldown_37_out));
  Add #(.Bits(32)) add_3 (.a(multiplexer_12_out), .b(multiplexer_13_out), .c_i(and_3_out), .s(add_3_s));  // open: c_o
  assign and_4_out = multiplexer_12_out & multiplexer_13_out;  // And and_4, 32 bits wide
  assign xor_1_out = multiplexer_12_out ^ multiplexer_13_out;  // XOr xor_1, 32 bits wide
  BarrelShifter #(.Bits(32)) barrelshifter_1 (
    .in(multiplexer_12_out), .shift(multiplexer_13_out[5:0]), .out(barrelshifter_1_out));
  BarrelShifter #(.Bits(32), .direction("right")) barrelshifter_2 (
    .in(multiplexer_12_out), .shift(multiplexer_13_out[5:0]), .out(barrelshifter_2_out));
  BarrelShifter #(.Bits(32), .barrelShifterMode("arithmetic"), .barrelSigned("true"), .direction("right")) barrelshifter_3 (
    .in(multiplexer_12_out), .shift(multiplexer_13_out[6:0]), .out(barrelshifter_3_out));
  Sub #(.Bits(32)) sub_2 (
    .a(multiplexer_12_out), .b(multiplexer_13_out), .c_i(pulldown_34_out), .s(sub_2_s), .c_o(sub_2_c_o[0]));
  assign or_7_out = multiplexer_12_out | multiplexer_13_out;  // Or or_7, 32 bits wide
  PullDown pulldown_38 (.out(rom_1_d[0]));
  Demultiplexer #(.Bits(32)) demultiplexer_10 (
    .sel(rom_1_d[16]), .in(add_2_s), .out_0(demultiplexer_10_out_0), .out_1(demultiplexer_10_out_1));
  assign MemoryAddressBus = rom_1_d[2] ? counterpreset_1_out : 32'bz;  // Driver driver_5
  Multiplexer #(.Bits(32)) multiplexer_14 (
    .sel(decoder_1_out_1), .in_0(d_ff_4_q), .in_1(RegINBus), .out(multiplexer_14_out));
  D_FF #(.Bits(32)) d_ff_4 (.D(multiplexer_14_out), .C(clk), .Q(d_ff_4_q));  // open: nQ
  Multiplexer #(.Bits(32)) multiplexer_15 (
    .sel(decoder_1_out_2), .in_0(d_ff_5_q), .in_1(RegINBus), .out(multiplexer_15_out));
  D_FF #(.Bits(32)) d_ff_5 (.D(multiplexer_15_out), .C(clk), .Q(d_ff_5_q));  // open: nQ
  Multiplexer #(.Bits(32)) multiplexer_16 (
    .sel(decoder_1_out_3), .in_0(d_ff_6_q), .in_1(RegINBus), .out(multiplexer_16_out));
  D_FF #(.Bits(32)) d_ff_6 (.D(multiplexer_16_out), .C(clk), .Q(d_ff_6_q));  // open: nQ
  Multiplexer #(.Bits(32)) multiplexer_17 (
    .sel(decoder_1_out_4), .in_0(d_ff_7_q), .in_1(RegINBus), .out(multiplexer_17_out));
  D_FF #(.Bits(32)) d_ff_7 (.D(multiplexer_17_out), .C(clk), .Q(d_ff_7_q));  // open: nQ
  Multiplexer #(.Bits(32)) multiplexer_18 (
    .sel(decoder_1_out_5), .in_0(d_ff_8_q), .in_1(RegINBus), .out(multiplexer_18_out));
  D_FF #(.Bits(32)) d_ff_8 (.D(multiplexer_18_out), .C(clk), .Q(d_ff_8_q));  // open: nQ
  Multiplexer #(.Bits(32)) multiplexer_19 (
    .sel(decoder_1_out_6), .in_0(d_ff_9_q), .in_1(RegINBus), .out(multiplexer_19_out));
  D_FF #(.Bits(32)) d_ff_9 (.D(multiplexer_19_out), .C(clk), .Q(d_ff_9_q));  // open: nQ
  Multiplexer #(.Bits(32)) multiplexer_20 (
    .sel(decoder_1_out_7), .in_0(d_ff_10_q), .in_1(RegINBus), .out(multiplexer_20_out));
  D_FF #(.Bits(32)) d_ff_10 (.D(multiplexer_20_out), .C(clk), .Q(d_ff_10_q));  // open: nQ
  Multiplexer #(.Bits(32)) multiplexer_21 (
    .sel(decoder_1_out_8), .in_0(d_ff_11_q), .in_1(RegINBus), .out(multiplexer_21_out));
  D_FF #(.Bits(32)) d_ff_11 (.D(multiplexer_21_out), .C(clk), .Q(d_ff_11_q));  // open: nQ
  Multiplexer #(.Bits(32)) multiplexer_22 (
    .sel(decoder_1_out_9), .in_0(d_ff_12_q), .in_1(RegINBus), .out(multiplexer_22_out));
  D_FF #(.Bits(32)) d_ff_12 (.D(multiplexer_22_out), .C(clk), .Q(d_ff_12_q));  // open: nQ
  Multiplexer #(.Bits(32)) multiplexer_23 (
    .sel(decoder_1_out_10), .in_0(d_ff_13_q), .in_1(RegINBus), .out(multiplexer_23_out));
  D_FF #(.Bits(32)) d_ff_13 (.D(multiplexer_23_out), .C(clk), .Q(d_ff_13_q));  // open: nQ
  Multiplexer #(.Bits(32)) multiplexer_24 (
    .sel(decoder_1_out_11), .in_0(d_ff_14_q), .in_1(RegINBus), .out(multiplexer_24_out));
  D_FF #(.Bits(32)) d_ff_14 (.D(multiplexer_24_out), .C(clk), .Q(d_ff_14_q));  // open: nQ
  Multiplexer #(.Bits(32)) multiplexer_25 (
    .sel(decoder_1_out_12), .in_0(d_ff_15_q), .in_1(RegINBus), .out(multiplexer_25_out));
  D_FF #(.Bits(32)) d_ff_15 (.D(multiplexer_25_out), .C(clk), .Q(d_ff_15_q));  // open: nQ
  Multiplexer #(.Bits(32)) multiplexer_26 (
    .sel(decoder_1_out_13), .in_0(d_ff_16_q), .in_1(RegINBus), .out(multiplexer_26_out));
  D_FF #(.Bits(32)) d_ff_16 (.D(multiplexer_26_out), .C(clk), .Q(d_ff_16_q));  // open: nQ
  Multiplexer #(.Bits(32)) multiplexer_27 (
    .sel(decoder_1_out_14), .in_0(d_ff_17_q), .in_1(RegINBus), .out(multiplexer_27_out));
  D_FF #(.Bits(32)) d_ff_17 (.D(multiplexer_27_out), .C(clk), .Q(d_ff_17_q));  // open: nQ
  Multiplexer #(.Bits(32)) multiplexer_28 (
    .sel(decoder_1_out_15), .in_0(d_ff_18_q), .in_1(RegINBus), .out(multiplexer_28_out));
  D_FF #(.Bits(32)) d_ff_18 (.D(multiplexer_28_out), .C(clk), .Q(d_ff_18_q));  // open: nQ
  PullDown #(.Bits(2)) pulldown_39 (.out(pulldown_39_out));
  PullDown #(.Bits(32)) pulldown_40 (.out(pulldown_40_out));
  assign MemoryOUTBus = demultiplexer_11_out_1 ? demultiplexer_10_out_1 : 32'bz;  // Driver driver_6
  assign RegINBus = demultiplexer_11_out_0 ? {demultiplexer_10_out_0[29:0], pulldown_39_out} : 32'bz;  // Driver driver_7
  assign OUT1 = decoder_2_out_0 ? pulldown_40_out : 32'bz;  // Driver driver_8
  assign OUT2 = decoder_3_out_0 ? pulldown_40_out : 32'bz;  // Driver driver_9
  assign OUT1 = decoder_2_out_1 ? d_ff_4_q : 32'bz;  // Driver driver_10
  assign OUT2 = decoder_3_out_1 ? d_ff_4_q : 32'bz;  // Driver driver_11
  assign OUT1 = decoder_2_out_2 ? d_ff_5_q : 32'bz;  // Driver driver_12
  assign OUT2 = decoder_3_out_2 ? d_ff_5_q : 32'bz;  // Driver driver_13
  assign OUT1 = decoder_2_out_3 ? d_ff_6_q : 32'bz;  // Driver driver_14
  assign OUT2 = decoder_3_out_3 ? d_ff_6_q : 32'bz;  // Driver driver_15
  assign OUT1 = decoder_2_out_4 ? d_ff_7_q : 32'bz;  // Driver driver_16
  assign OUT2 = decoder_3_out_4 ? d_ff_7_q : 32'bz;  // Driver driver_17
  assign OUT1 = decoder_2_out_5 ? d_ff_8_q : 32'bz;  // Driver driver_18
  assign OUT2 = decoder_3_out_5 ? d_ff_8_q : 32'bz;  // Driver driver_19
  assign OUT1 = decoder_2_out_6 ? d_ff_9_q : 32'bz;  // Driver driver_20
  assign OUT2 = decoder_3_out_6 ? d_ff_9_q : 32'bz;  // Driver driver_21
  assign OUT1 = decoder_2_out_7 ? d_ff_10_q : 32'bz;  // Driver driver_22
  assign OUT2 = decoder_3_out_7 ? d_ff_10_q : 32'bz;  // Driver driver_23
  assign OUT1 = decoder_2_out_8 ? d_ff_11_q : 32'bz;  // Driver driver_24
  assign OUT2 = decoder_3_out_8 ? d_ff_11_q : 32'bz;  // Driver driver_25
  assign OUT1 = decoder_2_out_9 ? d_ff_12_q : 32'bz;  // Driver driver_26
  assign OUT2 = decoder_3_out_9 ? d_ff_12_q : 32'bz;  // Driver driver_27
  assign OUT1 = decoder_2_out_10 ? d_ff_13_q : 32'bz;  // Driver driver_28
  assign OUT2 = decoder_3_out_10 ? d_ff_13_q : 32'bz;  // Driver driver_29
  assign OUT1 = decoder_2_out_11 ? d_ff_14_q : 32'bz;  // Driver driver_30
  assign OUT2 = decoder_3_out_11 ? d_ff_14_q : 32'bz;  // Driver driver_31
  assign OUT1 = decoder_2_out_12 ? d_ff_15_q : 32'bz;  // Driver driver_32
  assign OUT2 = decoder_3_out_12 ? d_ff_15_q : 32'bz;  // Driver driver_33
  assign OUT1 = decoder_2_out_13 ? d_ff_16_q : 32'bz;  // Driver driver_34
  assign OUT2 = decoder_3_out_13 ? d_ff_16_q : 32'bz;  // Driver driver_35
  assign OUT1 = decoder_2_out_14 ? d_ff_17_q : 32'bz;  // Driver driver_36
  assign OUT2 = decoder_3_out_14 ? d_ff_17_q : 32'bz;  // Driver driver_37
  assign OUT1 = decoder_2_out_15 ? d_ff_18_q : 32'bz;  // Driver driver_38
  assign OUT2 = decoder_3_out_15 ? d_ff_18_q : 32'bz;  // Driver driver_39
  Multiplexer #(.Selector_Bits(3), .Bits(32)) multiplexer_29 (
    .sel({rom_1_d[6], rom_1_d[7], rom_1_d[8]}), .in_0(add_3_s), .in_1(and_4_out), .in_2(xor_1_out),
    .in_3(barrelshifter_1_out), .in_4(barrelshifter_2_out), .in_5(barrelshifter_3_out), .in_6(sub_2_s),
    .in_7(or_7_out), .out(multiplexer_29_out));
  Demultiplexer demultiplexer_11 (
    .sel(rom_1_d[16]), .in(rom_1_d[12]), .out_0(demultiplexer_11_out_0), .out_1(demultiplexer_11_out_1));
  PullDown #(.Bits(31)) pulldown_41 (.out(pulldown_41_out));
  PullDown #(.Bits(31)) pulldown_42 (.out(pulldown_42_out));
  not not_5 (not_5_out[0], multiplexer_29_out[31]);
  PullDown #(.Bits(31)) pulldown_43 (.out(pulldown_43_out));
  not not_6 (not_6_out[0], sub_2_c_o[0]);
  PullDown #(.Bits(31)) pulldown_44 (.out(pulldown_44_out));
  assign {or_8_out_4, or_8_out_3, or_8_out_2, or_8_out} = multiplexer_29_out[7:0] | multiplexer_29_out[15:8] | multiplexer_29_out[23:16] | multiplexer_29_out[31:24];  // Or or_8, 8 bits wide
  PullDown #(.Bits(2)) pulldown_45 (.out(pulldown_45_out));
  not not_7 (not_7_out[0], or_9_out[0]);
  PullDown #(.Bits(31)) pulldown_46 (.out(pulldown_46_out));
  PullDown #(.Bits(31)) pulldown_47 (.out(pulldown_47_out));
  or or_9 (or_9_out[0], or_10_out[0], or_10_out[1]);
  Multiplexer #(.Selector_Bits(3), .Bits(32)) multiplexer_30 (
    .sel({rom_1_d[9], rom_1_d[10], rom_1_d[11]}), .in_0(multiplexer_29_out),
    .in_1({pulldown_42_out, multiplexer_29_out[31]}), .in_2({pulldown_41_out, sub_2_c_o[0]}),
    .in_3({multiplexer_29_out[29:0], pulldown_45_out}), .in_4({pulldown_43_out, not_5_out[0]}),
    .in_5({pulldown_44_out, not_6_out[0]}), .in_6({pulldown_46_out, not_7_out[0]}),
    .in_7({pulldown_47_out, or_9_out[0]}), .out(multiplexer_30_out));
  assign or_10_out = or_8_out | or_8_out_2 | or_8_out_3 | or_8_out_4;  // Or or_10, 2 bits wide
  Decoder #(.Selector_Bits(4)) decoder_2 (
    .sel(demultiplexer_6_out_0[3:0]), .out_0(decoder_2_out_0), .out_1(decoder_2_out_1),
    .out_2(decoder_2_out_2), .out_3(decoder_2_out_3), .out_4(decoder_2_out_4), .out_5(decoder_2_out_5),
    .out_6(decoder_2_out_6), .out_7(decoder_2_out_7), .out_8(decoder_2_out_8), .out_9(decoder_2_out_9),
    .out_10(decoder_2_out_10), .out_11(decoder_2_out_11), .out_12(decoder_2_out_12),
    .out_13(decoder_2_out_13), .out_14(decoder_2_out_14), .out_15(decoder_2_out_15));
  Decoder #(.Selector_Bits(4)) decoder_3 (
    .sel(demultiplexer_5_out_1[3:0]), .out_0(decoder_3_out_0), .out_1(decoder_3_out_1),
    .out_2(decoder_3_out_2), .out_3(decoder_3_out_3), .out_4(decoder_3_out_4), .out_5(decoder_3_out_5),
    .out_6(decoder_3_out_6), .out_7(decoder_3_out_7), .out_8(decoder_3_out_8), .out_9(decoder_3_out_9),
    .out_10(decoder_3_out_10), .out_11(decoder_3_out_11), .out_12(decoder_3_out_12),
    .out_13(decoder_3_out_13), .out_14(decoder_3_out_14), .out_15(decoder_3_out_15));
  assign RegINBus = decoder_4_out_3 ? multiplexer_30_out : 32'bz;  // Driver driver_40
  assign MemoryOUTBus = decoder_4_out_2 ? multiplexer_30_out : 32'bz;  // Driver driver_41
  assign MemoryAddressBus = decoder_4_out_1 ? multiplexer_30_out : 32'bz;  // Driver driver_42
  Decoder #(.Selector_Bits(2)) decoder_4 (
    .sel({rom_1_d[13], rom_1_d[15]}), .out_1(decoder_4_out_1), .out_2(decoder_4_out_2),
    .out_3(decoder_4_out_3));  // open: out_0

  assign out_9 = MemoryAddressBus[31:20];

  // Notes on the sheet:
  //   clk: Hz: 500
  //   HLT: default 1
  //   R type
  //   ~I_type
  //   This is here because 
  //   only the last
  //   field differs in 
  //   R/S/B types.
  //   NOOP here can also be used as a way
  //   to defer LOAD-ing to the next 
  //   instruction (a.k.a creating a 
  //   pipeline stall) to the next cycle 
  //   if the current instruction needs 
  //   access to ram in some way which 
  //   can not be done in parallel with LOAD.
  //   I type
  //   J type
  //   LOAD_IR
  //   U type
  //   Pipeline / Instruction Register
  //   IR2
  //   U/J type
  //   RD(5)
  //   Control Logic
  //   RS1(5)
  //   RS2(5)
  //   proper B type 
  //   handling
  //   proper J type 
  //   handling
  //   IR1
  //   Decoding UNIT
  //   S/B type
  //   IMM(32)
  //   ID
  //   NOTE:
  //   If you don't want the first
  //   instruction to be skipped
  //   you should pulse the clock
  //   once ( technically you only need a
  //   low to high clock edge )
  //    wihile in HLT to fill the IRs (a.k.a pipeline)
  //   funct7
  //   funct3
  //   Control signals change on the
  //   down-clock, since that's
  //   when we DECODE.
  //   We EXECUTE and FETCH on
  //   the up-clock.
  //   This muxer is here
  //   to stop the cpu from
  //   executing the instruction
  //   that is cached in the IRs
  //   while in RST. To achive that
  //   it replaces all instructions
  //   that sould have otherwise 
  //   gone to the decoder 
  //   with NOOps.
  //   B type
  //   High bit
  //   Low nibble
  //   contents of rom_1 (hex, n*v repeats v):
  //   80005,80005,80005,80005,aa005,2aac35,80005,80005,80005,80005,80005,80005,8e005,6a0005,
  //   80005,80005,80005,80005,80005,80005,80005,80005,80005,80005,7f687,6302f,80005,63037,
  //   80005,80005,80005,80005,80005,80005,80005,80005,aa005,2aac35,80005,80005,80005,80005,
  //   80005,80005,8e0c5,6a0005,80005,80005,80005,80005,80005,80005,80005,80005,80005,80005,
  //   7f687,6302f,80005,63037,80005,80005,80005,80005,80005,80005,80005,80005,aa185,2aac35,
  //   80005,80005,80005,80005,80005,80005,8e185,6a0005,80005,80005,80005,80005,80005,80005,
  //   80005,80005,80005,80005,7fe87,6302f,80005,63037,80005,80005,80005,80005,80005,80005,
  //   80005,80005,aa185,2aac35,80005,80005,80005,80005,80005,80005,8e185,6a0005,80005,80005,
  //   80005,80005,80005,80005,80005,80005,80005,80005,7fe87,6302f,80005,63037,80005,80005,
  //   80005,80005,8e8028,80005,80005,80005,aa8c5,2aac35,80005,80005,1168028,80005,80005,
  //   80005,8e8c5,6a0005,80005,80005,80005,80005,80005,80005,80005,80005,80005,80005,80005,
  //   6302f,80005,63037,80005,80005,80005,80005,8e8028,80005,80005,80005,aa8c5,2aac35,80005,
  //   80005,1168028,80005,80005,80005,8e8c5,6a0005,80005,80005,80005,80005,80005,80005,
  //   80005,80005,80005,80005,80005,6302f,80005,63037,80005,80005,80005,80005,80005,80005,
  //   80005,80005,aa4c5,2aac35,80005,80005,80005,80005,80005,80005,8e4c5,6a0005,80005,80005,
  //   80005,80005,80005,80005,80005,80005,80005,80005,80005,6302f,80005,63037,80005,80005,
  //   80005,80005,80005,80005,80005,80005,aa4c5,2aac35,80005,80005,80005,80005,80005,80005,
  //   8e4c5,6a0005,80005,80005,80005,80005,80005,80005,80005,80005,80005,80005,80005,6302f,
  //   80005,63037,80005,80005,80005,80005,80005,80005,80005,80005,aa085,2aac35,80005,80005,
  //   80005,80005,80005,80005,8e085,6a0005,80005,80005,80005,80005,80005,80005,80005,80005,
  //   80005,80005,7f8c7,6302f,80005,63037,80005,80005,80005,80005,80005,80005,80005,80005,
  //   aa085,2aac35,80005,80005,80005,80005,80005,80005,8e085,6a0005,80005,80005,80005,80005,
  //   80005,80005,80005,80005,80005,80005,7f8c7,6302f,80005,63037,80005,80005,80005,80005,
  //   80005,80005,80005,80005,aa045,2aac35,80005,80005,80005,80005,80005,80005,8e045,6a0005,
  //   80005,80005,80005,80005,80005,80005,80005,80005,80005,80005,7f2c7,6302f,80005,63037,
  //   80005,80005,80005,80005,80005,80005,80005,80005,aa145,2aac35,80005,80005,80005,80005,
  //   80005,80005,8e145,6a0005,80005,80005,80005,80005,80005,80005,80005,80005,80005,80005,
  //   7f2c7,6302f,80005,63037,80005,80005,80005,80005,80005,80005,80005,80005,aa1c5,2aac35,
  //   80005,80005,80005,80005,80005,80005,8e1c5,6a0005,80005,80005,80005,80005,80005,80005,
  //   80005,80005,80005,80005,7f4c7,6302f,80005,63037,80005,80005,80005,80005,80005,80005,
  //   80005,80005,aa1c5,2aac35,80005,80005,80005,80005,80005,80005,8e1c5,6a0005,80005,80005,
  //   80005,80005,80005,80005,80005,80005,80005,80005,7f4c7,6302f,80005,63037,80005,80005,
  //   80005,80005,80005,80005,80005,80005,aa105,2aac35,80005,80005,80005,80005,80005,80005,
  //   8e105,6a0005,80005,80005,80005,80005,80005,80005,80005,80005,80005,80005,7fac7,6302f,
  //   80005,63037,80005,80005,80005,80005,80005,80005,80005,80005,aa105,2aac35,80005,80005,
  //   80005,80005,80005,80005,8e105,6a0005,80005,80005,80005,80005,80005,80005,80005,80005,
  //   80005,80005,7fac7,6302f,80005,63037,80005,80005,80005,80005
  //   Control Lines
  //   MOUTB TO RINB
  //   REG_OUT
  //   CNTRL_UPIMM
  //   ROUTB TO RINB
  //   Hack for
  //   I immediate
  //   in SRAI/SRLI
  //   RAM_ENO
  //   RAM_LOAD
  //   CNTRL_IMM_OUT
  //   IR_NOP
  //   ALU__OUT B0
  //   AAU_SWTCHMOD
  //   ALU_SWTCHB_REG
  //   ALU_OUT B1
  //   ALU_OUTMOD B0
  //   AAU_OUT
  //   Hardcoded arithmetic 
  //   shift right by 2.
  //   Translates byte offset to
  //   native offset.
  //   Hardcoded logical 
  //   shift right by 2.
  //   Translates byte address to
  //   native address.
  //   ALU_OUTMOD B1
  //   ALU_OUTMOD B2
  //   Hack for 
  //   jumps/branches,
  //   for pipeline
  //   stall (nop)
  //   ALU_OP B0
  //   ALU_OP B1
  //   ALU_TRANSB
  //   ALU_OP B2
  //   HLT can only be changed
  //   on the down-clock so the
  //   instruction which is cached in the
  //   irs ( a.k.a the first instruction )
  //   gets to be parsed instead of
  //   acting like a no-op.
  //   If HLT were to change
  //   on a high clock
  //   then there would have
  //   never been a down clock before
  //   it, which means the cpu
  //   didn't load the instruction
  //   even though it thinks so
  //   which causes it to skip
  //   over it.
  //   Address Arithmetic UNIT
  //   Enables input, but also enables counting,
  //   but if load is on it will latch the value
  //   instead of counting
  //   ALU_SWTCHA B0
  //   ALU_SWTCHA B1
  //   Register File
  //   RS1
  //   IMM/RS2
  //   PC_OUT
  //   PC_LOAD
  //   PC
  //   PC_ENIN/_ENC
  //   Arithmetic and Logic UNIT
  //   CLK
  //   SUBC
  //   SIGNBIT
  //   Hardcoded
  //   shift left by 2.
  //   Translate native address
  //   to byte oriented address
  //   .
  //   Note: yes, there is a difference
  //   between testing wheter the 
  //   result is negative (a.k.a sign bit is 1)
  //   and looking at wheter the
  //   carry out of subtraction is set.
  //   that differance occurs, 
  //   when dealing with unsigned 
  //   numbers  that use the first bit,
  //   because 0xFFFFFFFF. is negative in 
  //   32-bit 2's complement but positive 
  //   if treated as unsigned so 
  //   basically the carry out of
  //   subtraction is a little like
  //   the sign bit of a 33-bit
  //   adder where the second
  //   input is inverted and Cin is on,
  //   i think.
  //   This differnce was encountered when
  //   implementing SLTI and SLTIU.
  //   SEL1
  //   SEL2
endmodule
